// Digital circuit block_function.dig as structural Verilog
module block_function (
  input  [31:0] k0,
  input  [31:0] k1,
  input  [31:0] k2,
  input  [31:0] k3,
  input  [31:0] k4,
  input  [31:0] k5,
  input  [31:0] k6,
  input  [31:0] k7,
  input  [31:0] bc,
  input  [31:0] n0,
  input  [31:0] n1,
  input  [31:0] n2,
  input  start,
  input  clk,
  output [31:0] o0,
  output [31:0] o1,
  output [31:0] o2,
  output [31:0] o3,
  output [31:0] o4,
  output [31:0] o5,
  output [31:0] o6,
  output [31:0] o7,
  output [31:0] o8,
  output [31:0] o9,
  output [31:0] o10,
  output [31:0] o11,
  output [31:0] o12,
  output [31:0] o13,
  output [31:0] o14,
  output [31:0] o15,
  output done
);

  wire en, ndone, r10, run, step;
  wire [3:0] multiplexer_17_out, r, rnext;
  wire [31:0] bcl, ib0, ib1, ib2, ib3, ib4, ib5, ib6, ib7, ib8, ib9, ib10, ib11, ib12, ib13, ib14, ib15, m0,
       m1, m2, m3, m4, m5, m6, m7, m8, m9, m10, m11, m12, m13, m14, m15, s0, s1, s2, s3, s4, s5, s6, s7, s8,
       s9, s10, s11, s12, s13, s14, s15;

  Add #(.Bits(32)) add_1 (.a(32'h61707865), .b(s0), .c_i(1'b0), .s(o0));  // open: c_o
  Add #(.Bits(32)) add_2 (.a(32'h3320646e), .b(s1), .c_i(1'b0), .s(o1));  // open: c_o
  Add #(.Bits(32)) add_3 (.a(32'h79622d32), .b(s2), .c_i(1'b0), .s(o2));  // open: c_o
  Add #(.Bits(32)) add_4 (.a(32'h6b206574), .b(s3), .c_i(1'b0), .s(o3));  // open: c_o
  Add #(.Bits(32)) add_5 (.a(k0), .b(s4), .c_i(1'b0), .s(o4));  // open: c_o
  Add #(.Bits(32)) add_6 (.a(k1), .b(s5), .c_i(1'b0), .s(o5));  // open: c_o
  Add #(.Bits(32)) add_7 (.a(k2), .b(s6), .c_i(1'b0), .s(o6));  // open: c_o
  Add #(.Bits(32)) add_8 (.a(k3), .b(s7), .c_i(1'b0), .s(o7));  // open: c_o
  Add #(.Bits(32)) add_9 (.a(k4), .b(s8), .c_i(1'b0), .s(o8));  // open: c_o
  Add #(.Bits(32)) add_10 (.a(k5), .b(s9), .c_i(1'b0), .s(o9));  // open: c_o
  Add #(.Bits(32)) add_11 (.a(k6), .b(s10), .c_i(1'b0), .s(o10));  // open: c_o
  Add #(.Bits(32)) add_12 (.a(k7), .b(s11), .c_i(1'b0), .s(o11));  // open: c_o
  Add #(.Bits(32)) add_13 (.a(bcl), .b(s12), .c_i(1'b0), .s(o12));  // open: c_o
  Add #(.Bits(32)) add_14 (.a(n0), .b(s13), .c_i(1'b0), .s(o13));  // open: c_o
  Add #(.Bits(32)) add_15 (.a(n1), .b(s14), .c_i(1'b0), .s(o14));  // open: c_o
  Add #(.Bits(32)) add_16 (.a(n2), .b(s15), .c_i(1'b0), .s(o15));  // open: c_o
  // inner_block_function inner_block_function_1: pin names not known; wires that end beside it: m0, m1, m2, m3, m4, m5, m6, m7, m8, m9, m10, m11, m12, m13, m14, m15, ib0, ib1, ib2, ib3, ib4, ib5, ib6, ib7, ib8, ib9, ib10, ib11, ib12, ib13, ib14, ib15
  Multiplexer #(.Bits(32)) multiplexer_1 (.sel(start), .in_0(s0), .in_1(32'h61707865), .out(m0));
  Multiplexer #(.Bits(32)) multiplexer_2 (.sel(start), .in_0(s1), .in_1(32'h3320646e), .out(m1));
  Multiplexer #(.Bits(32)) multiplexer_3 (.sel(start), .in_0(s2), .in_1(32'h79622d32), .out(m2));
  Multiplexer #(.Bits(32)) multiplexer_4 (.sel(start), .in_0(s3), .in_1(32'h6b206574), .out(m3));
  Multiplexer #(.Bits(32)) multiplexer_5 (.sel(start), .in_0(s4), .in_1(k0), .out(m4));
  Multiplexer #(.Bits(32)) multiplexer_6 (.sel(start), .in_0(s5), .in_1(k1), .out(m5));
  Multiplexer #(.Bits(32)) multiplexer_7 (.sel(start), .in_0(s6), .in_1(k2), .out(m6));
  Multiplexer #(.Bits(32)) multiplexer_8 (.sel(start), .in_0(s7), .in_1(k3), .out(m7));
  Multiplexer #(.Bits(32)) multiplexer_9 (.sel(start), .in_0(s8), .in_1(k4), .out(m8));
  Multiplexer #(.Bits(32)) multiplexer_10 (.sel(start), .in_0(s9), .in_1(k5), .out(m9));
  Multiplexer #(.Bits(32)) multiplexer_11 (.sel(start), .in_0(s10), .in_1(k6), .out(m10));
  Multiplexer #(.Bits(32)) multiplexer_12 (.sel(start), .in_0(s11), .in_1(k7), .out(m11));
  Multiplexer #(.Bits(32)) multiplexer_13 (.sel(start), .in_0(s12), .in_1(bc), .out(m12));
  Multiplexer #(.Bits(32)) multiplexer_14 (.sel(start), .in_0(s13), .in_1(n0), .out(m13));
  Multiplexer #(.Bits(32)) multiplexer_15 (.sel(start), .in_0(s14), .in_1(n1), .out(m14));
  Multiplexer #(.Bits(32)) multiplexer_16 (.sel(start), .in_0(s15), .in_1(n2), .out(m15));
  Register #(.Bits(32)) u_S0 (.D(ib0), .C(clk), .en(en), .Q(s0));
  Register #(.Bits(32)) u_S1 (.D(ib1), .C(clk), .en(en), .Q(s1));
  Register #(.Bits(32)) u_S2 (.D(ib2), .C(clk), .en(en), .Q(s2));
  Register #(.Bits(32)) u_S3 (.D(ib3), .C(clk), .en(en), .Q(s3));
  Register #(.Bits(32)) u_S4 (.D(ib4), .C(clk), .en(en), .Q(s4));
  Register #(.Bits(32)) u_S5 (.D(ib5), .C(clk), .en(en), .Q(s5));
  Register #(.Bits(32)) u_S6 (.D(ib6), .C(clk), .en(en), .Q(s6));
  Register #(.Bits(32)) u_S7 (.D(ib7), .C(clk), .en(en), .Q(s7));
  Register #(.Bits(32)) u_S8 (.D(ib8), .C(clk), .en(en), .Q(s8));
  Register #(.Bits(32)) u_S9 (.D(ib9), .C(clk), .en(en), .Q(s9));
  Register #(.Bits(32)) u_S10 (.D(ib10), .C(clk), .en(en), .Q(s10));
  Register #(.Bits(32)) u_S11 (.D(ib11), .C(clk), .en(en), .Q(s11));
  Register #(.Bits(32)) u_S12 (.D(ib12), .C(clk), .en(en), .Q(s12));
  Register #(.Bits(32)) u_S13 (.D(ib13), .C(clk), .en(en), .Q(s13));
  Register #(.Bits(32)) u_S14 (.D(ib14), .C(clk), .en(en), .Q(s14));
  Register #(.Bits(32)) u_S15 (.D(ib15), .C(clk), .en(en), .Q(s15));
  D_FF u_run (.D(en), .C(clk), .Q(run));  // open: nQ
  Comparator #(.Bits(4)) comparator_1 (.a(r), .b(4'b1010), .eq(r10));  // open: gt, lt
  and and_1 (done, run, r10);
  not not_1 (ndone, done);
  and and_2 (step, run, ndone);
  or or_1 (en, start, step);
  Add #(.Bits(4)) add_17 (.a(r), .b(4'b0001), .c_i(1'b0), .s(rnext));  // open: c_o
  Multiplexer #(.Bits(4)) multiplexer_17 (.sel(start), .in_0(rnext), .in_1(4'b0001), .out(multiplexer_17_out));
  Register #(.Bits(4)) u_r (.D(multiplexer_17_out), .C(clk), .en(en), .Q(r));
  Register #(.Bits(32)) u_bcl (.D(bc), .C(clk), .en(start), .Q(bcl));
endmodule

/* Test case test0:
k0 k1 k2 k3 k4 k5 k6 k7 bc n0 n1 n2 start clk   o0 o1 o2 o3 o4 o5 o6 o7 o8 o9 o10 o11 o12 o13 o14 o15 done

# idle
0x03020100 0x07060504 0x0b0a0908 0x0f0e0d0c 0x13121110 0x17161514 0x1b1a1918 0x1f1e1d1c 0x00000001 0x09000000 0x4a000000 0x00000000 0 0   X X X X X X X X X X X X X X X X 0
# clock 1: start pulse, initial state + double round 1
0x03020100 0x07060504 0x0b0a0908 0x0f0e0d0c 0x13121110 0x17161514 0x1b1a1918 0x1f1e1d1c 0x00000001 0x09000000 0x4a000000 0x00000000 1 C   X X X X X X X X X X X X X X X X 0
# clocks 2-9: double rounds 2-9
0x03020100 0x07060504 0x0b0a0908 0x0f0e0d0c 0x13121110 0x17161514 0x1b1a1918 0x1f1e1d1c 0x00000001 0x09000000 0x4a000000 0x00000000 0 C   X X X X X X X X X X X X X X X X 0
0x03020100 0x07060504 0x0b0a0908 0x0f0e0d0c 0x13121110 0x17161514 0x1b1a1918 0x1f1e1d1c 0x00000001 0x09000000 0x4a000000 0x00000000 0 C   X X X X X X X X X X X X X X X X 0
0x03020100 0x07060504 0x0b0a0908 0x0f0e0d0c 0x13121110 0x17161514 0x1b1a1918 0x1f1e1d1c 0x00000001 0x09000000 0x4a000000 0x00000000 0 C   X X X X X X X X X X X X X X X X 0
0x03020100 0x07060504 0x0b0a0908 0x0f0e0d0c 0x13121110 0x17161514 0x1b1a1918 0x1f1e1d1c 0x00000001 0x09000000 0x4a000000 0x00000000 0 C   X X X X X X X X X X X X X X X X 0
0x03020100 0x07060504 0x0b0a0908 0x0f0e0d0c 0x13121110 0x17161514 0x1b1a1918 0x1f1e1d1c 0x00000001 0x09000000 0x4a000000 0x00000000 0 C   X X X X X X X X X X X X X X X X 0
0x03020100 0x07060504 0x0b0a0908 0x0f0e0d0c 0x13121110 0x17161514 0x1b1a1918 0x1f1e1d1c 0x00000001 0x09000000 0x4a000000 0x00000000 0 C   X X X X X X X X X X X X X X X X 0
0x03020100 0x07060504 0x0b0a0908 0x0f0e0d0c 0x13121110 0x17161514 0x1b1a1918 0x1f1e1d1c 0x00000001 0x09000000 0x4a000000 0x00000000 0 C   X X X X X X X X X X X X X X X X 0
0x03020100 0x07060504 0x0b0a0908 0x0f0e0d0c 0x13121110 0x17161514 0x1b1a1918 0x1f1e1d1c 0x00000001 0x09000000 0x4a000000 0x00000000 0 C   X X X X X X X X X X X X X X X X 0
# clock 10: double round 10, keystream ready
0x03020100 0x07060504 0x0b0a0908 0x0f0e0d0c 0x13121110 0x17161514 0x1b1a1918 0x1f1e1d1c 0x00000001 0x09000000 0x4a000000 0x00000000 0 C   0xe4e7f110 0x15593bd1 0x1fdd0f50 0xc47120a3 0xc7f4d1c7 0x0368c033 0x9aaa2204 0x4e6cd4c3 0x466482d2 0x09aa9f07 0x05d7c214 0xa2028bd9 0xd19c12b5 0xb94e16de 0xe883d0cb 0x4e3c50a2 1
# done lasts one clock, the outputs hold until the next start
0x03020100 0x07060504 0x0b0a0908 0x0f0e0d0c 0x13121110 0x17161514 0x1b1a1918 0x1f1e1d1c 0x00000001 0x09000000 0x4a000000 0x00000000 0 C   0xe4e7f110 0x15593bd1 0x1fdd0f50 0xc47120a3 0xc7f4d1c7 0x0368c033 0x9aaa2204 0x4e6cd4c3 0x466482d2 0x09aa9f07 0x05d7c214 0xa2028bd9 0xd19c12b5 0xb94e16de 0xe883d0cb 0x4e3c50a2 0
0x03020100 0x07060504 0x0b0a0908 0x0f0e0d0c 0x13121110 0x17161514 0x1b1a1918 0x1f1e1d1c 0x00000001 0x09000000 0x4a000000 0x00000000 0 C   0xe4e7f110 0x15593bd1 0x1fdd0f50 0xc47120a3 0xc7f4d1c7 0x0368c033 0x9aaa2204 0x4e6cd4c3 0x466482d2 0x09aa9f07 0x05d7c214 0xa2028bd9 0xd19c12b5 0xb94e16de 0xe883d0cb 0x4e3c50a2 0
# restart in the middle of a computation: start again from scratch
0x03020100 0x07060504 0x0b0a0908 0x0f0e0d0c 0x13121110 0x17161514 0x1b1a1918 0x1f1e1d1c 0x00000001 0x09000000 0x4a000000 0x00000000 1 C   X X X X X X X X X X X X X X X X 0
0x03020100 0x07060504 0x0b0a0908 0x0f0e0d0c 0x13121110 0x17161514 0x1b1a1918 0x1f1e1d1c 0x00000001 0x09000000 0x4a000000 0x00000000 0 C   X X X X X X X X X X X X X X X X 0
0x03020100 0x07060504 0x0b0a0908 0x0f0e0d0c 0x13121110 0x17161514 0x1b1a1918 0x1f1e1d1c 0x00000001 0x09000000 0x4a000000 0x00000000 0 C   X X X X X X X X X X X X X X X X 0
0x03020100 0x07060504 0x0b0a0908 0x0f0e0d0c 0x13121110 0x17161514 0x1b1a1918 0x1f1e1d1c 0x00000001 0x09000000 0x4a000000 0x00000000 0 C   X X X X X X X X X X X X X X X X 0
0x03020100 0x07060504 0x0b0a0908 0x0f0e0d0c 0x13121110 0x17161514 0x1b1a1918 0x1f1e1d1c 0x00000001 0x09000000 0x4a000000 0x00000000 0 C   X X X X X X X X X X X X X X X X 0
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*/

/* Test case A.1 #1:
k0 k1 k2 k3 k4 k5 k6 k7 bc n0 n1 n2 start clk   o0 o1 o2 o3 o4 o5 o6 o7 o8 o9 o10 o11 o12 o13 o14 o15 done

# RFC 8439 A.1, test vector #1: block counter 0
0x00000000 0x00000000 0x00000000 0x00000000 0x00000000 0x00000000 0x00000000 0x00000000 0x00000000 0x00000000 0x00000000 0x00000000 1 C   X X X X X X X X X X X X X X X X 0
0x00000000 0x00000000 0x00000000 0x00000000 0x00000000 0x00000000 0x00000000 0x00000000 0x00000000 0x00000000 0x00000000 0x00000000 0 C   X X X X X X X X X X X X X X X X 0
0x00000000 0x00000000 0x00000000 0x00000000 0x00000000 0x00000000 0x00000000 0x00000000 0x00000000 0x00000000 0x00000000 0x00000000 0 C   X X X X X X X X X X X X X X X X 0
0x00000000 0x00000000 0x00000000 0x00000000 0x00000000 0x00000000 0x00000000 0x00000000 0x00000000 0x00000000 0x00000000 0x00000000 0 C   X X X X X X X X X X X X X X X X 0
0x00000000 0x00000000 0x00000000 0x00000000 0x00000000 0x00000000 0x00000000 0x00000000 0x00000000 0x00000000 0x00000000 0x00000000 0 C   X X X X X X X X X X X X X X X X 0
0x00000000 0x00000000 0x00000000 0x00000000 0x00000000 0x00000000 0x00000000 0x00000000 0x00000000 0x00000000 0x00000000 0x00000000 0 C   X X X X X X X X X X X X X X X X 0
0x00000000 0x00000000 0x00000000 0x00000000 0x00000000 0x00000000 0x00000000 0x00000000 0x00000000 0x00000000 0x00000000 0x00000000 0 C   X X X X X X X X X X X X X X X X 0
0x00000000 0x00000000 0x00000000 0x00000000 0x00000000 0x00000000 0x00000000 0x00000000 0x00000000 0x00000000 0x00000000 0x00000000 0 C   X X X X X X X X X X X X X X X X 0
0x00000000 0x00000000 0x00000000 0x00000000 0x00000000 0x00000000 0x00000000 0x00000000 0x00000000 0x00000000 0x00000000 0x00000000 0 C   X X X X X X X X X X X X X X X X 0
0x00000000 0x00000000 0x00000000 0x00000000 0x00000000 0x00000000 0x00000000 0x00000000 0x00000000 0x00000000 0x00000000 0x00000000 0 C   0xade0b876 0x903df1a0 0xe56a5d40 0x28bd8653 0xb819d2bd 0x1aed8da0 0xccef36a8 0xc70d778b 0x7c5941da 0x8d485751 0x3fe02477 0x374ad8b8 0xf4b8436a 0x1ca11815 0x69b687c3 0x8665eeb2 1
*/

/* Test case A.1 #2:
k0 k1 k2 k3 k4 k5 k6 k7 bc n0 n1 n2 start clk   o0 o1 o2 o3 o4 o5 o6 o7 o8 o9 o10 o11 o12 o13 o14 o15 done

# RFC 8439 A.1, test vector #2: block counter 1
0x00000000 0x00000000 0x00000000 0x00000000 0x00000000 0x00000000 0x00000000 0x00000000 0x00000001 0x00000000 0x00000000 0x00000000 1 C   X X X X X X X X X X X X X X X X 0
0x00000000 0x00000000 0x00000000 0x00000000 0x00000000 0x00000000 0x00000000 0x00000000 0x00000001 0x00000000 0x00000000 0x00000000 0 C   X X X X X X X X X X X X X X X X 0
0x00000000 0x00000000 0x00000000 0x00000000 0x00000000 0x00000000 0x00000000 0x00000000 0x00000001 0x00000000 0x00000000 0x00000000 0 C   X X X X X X X X X X X X X X X X 0
0x00000000 0x00000000 0x00000000 0x00000000 0x00000000 0x00000000 0x00000000 0x00000000 0x00000001 0x00000000 0x00000000 0x00000000 0 C   X X X X X X X X X X X X X X X X 0
0x00000000 0x00000000 0x00000000 0x00000000 0x00000000 0x00000000 0x00000000 0x00000000 0x00000001 0x00000000 0x00000000 0x00000000 0 C   X X X X X X X X X X X X X X X X 0
0x00000000 0x00000000 0x00000000 0x00000000 0x00000000 0x00000000 0x00000000 0x00000000 0x00000001 0x00000000 0x00000000 0x00000000 0 C   X X X X X X X X X X X X X X X X 0
0x00000000 0x00000000 0x00000000 0x00000000 0x00000000 0x00000000 0x00000000 0x00000000 0x00000001 0x00000000 0x00000000 0x00000000 0 C   X X X X X X X X X X X X X X X X 0
0x00000000 0x00000000 0x00000000 0x00000000 0x00000000 0x00000000 0x00000000 0x00000000 0x00000001 0x00000000 0x00000000 0x00000000 0 C   X X X X X X X X X X X X X X X X 0
0x00000000 0x00000000 0x00000000 0x00000000 0x00000000 0x00000000 0x00000000 0x00000000 0x00000001 0x00000000 0x00000000 0x00000000 0 C   X X X X X X X X X X X X X X X X 0
0x00000000 0x00000000 0x00000000 0x00000000 0x00000000 0x00000000 0x00000000 0x00000000 0x00000001 0x00000000 0x00000000 0x00000000 0 C   0xbee7079f 0x7a385155 0x7c97ba98 0x0d082d73 0xa0290fcb 0x6965e348 0x3e53c612 0xed7aee32 0x7621b729 0x434ee69c 0xb03371d5 0xd539d874 0x281fed31 0x45fb0a51 0x1f0ae1ac 0x6f4d794b 1
*/

/* Test case A.1 #3:
k0 k1 k2 k3 k4 k5 k6 k7 bc n0 n1 n2 start clk   o0 o1 o2 o3 o4 o5 o6 o7 o8 o9 o10 o11 o12 o13 o14 o15 done

# RFC 8439 A.1, test vector #3: block counter 1
0x00000000 0x00000000 0x00000000 0x00000000 0x00000000 0x00000000 0x00000000 0x01000000 0x00000001 0x00000000 0x00000000 0x00000000 1 C   X X X X X X X X X X X X X X X X 0
0x00000000 0x00000000 0x00000000 0x00000000 0x00000000 0x00000000 0x00000000 0x01000000 0x00000001 0x00000000 0x00000000 0x00000000 0 C   X X X X X X X X X X X X X X X X 0
0x00000000 0x00000000 0x00000000 0x00000000 0x00000000 0x00000000 0x00000000 0x01000000 0x00000001 0x00000000 0x00000000 0x00000000 0 C   X X X X X X X X X X X X X X X X 0
0x00000000 0x00000000 0x00000000 0x00000000 0x00000000 0x00000000 0x00000000 0x01000000 0x00000001 0x00000000 0x00000000 0x00000000 0 C   X X X X X X X X X X X X X X X X 0
0x00000000 0x00000000 0x00000000 0x00000000 0x00000000 0x00000000 0x00000000 0x01000000 0x00000001 0x00000000 0x00000000 0x00000000 0 C   X X X X X X X X X X X X X X X X 0
0x00000000 0x00000000 0x00000000 0x00000000 0x00000000 0x00000000 0x00000000 0x01000000 0x00000001 0x00000000 0x00000000 0x00000000 0 C   X X X X X X X X X X X X X X X X 0
0x00000000 0x00000000 0x00000000 0x00000000 0x00000000 0x00000000 0x00000000 0x01000000 0x00000001 0x00000000 0x00000000 0x00000000 0 C   X X X X X X X X X X X X X X X X 0
0x00000000 0x00000000 0x00000000 0x00000000 0x00000000 0x00000000 0x00000000 0x01000000 0x00000001 0x00000000 0x00000000 0x00000000 0 C   X X X X X X X X X X X X X X X X 0
0x00000000 0x00000000 0x00000000 0x00000000 0x00000000 0x00000000 0x00000000 0x01000000 0x00000001 0x00000000 0x00000000 0x00000000 0 C   X X X X X X X X X X X X X X X X 0
0x00000000 0x00000000 0x00000000 0x00000000 0x00000000 0x00000000 0x00000000 0x01000000 0x00000001 0x00000000 0x00000000 0x00000000 0 C   0x2452eb3a 0x9249f8ec 0x8d829d9b 0xddd4ceb1 0xe8252083 0x60818b01 0xf38422b8 0x5aaa49c9 0xbb00ca8e 0xda3ba7b4 0xc4b592d1 0xfdf2732f 0x4436274e 0x2561b3c8 0xebdd4aa6 0xa0136c00 1
*/

/* Test case A.1 #4:
k0 k1 k2 k3 k4 k5 k6 k7 bc n0 n1 n2 start clk   o0 o1 o2 o3 o4 o5 o6 o7 o8 o9 o10 o11 o12 o13 o14 o15 done

# RFC 8439 A.1, test vector #4: block counter 2
0x0000ff00 0x00000000 0x00000000 0x00000000 0x00000000 0x00000000 0x00000000 0x00000000 0x00000002 0x00000000 0x00000000 0x00000000 1 C   X X X X X X X X X X X X X X X X 0
0x0000ff00 0x00000000 0x00000000 0x00000000 0x00000000 0x00000000 0x00000000 0x00000000 0x00000002 0x00000000 0x00000000 0x00000000 0 C   X X X X X X X X X X X X X X X X 0
0x0000ff00 0x00000000 0x00000000 0x00000000 0x00000000 0x00000000 0x00000000 0x00000000 0x00000002 0x00000000 0x00000000 0x00000000 0 C   X X X X X X X X X X X X X X X X 0
0x0000ff00 0x00000000 0x00000000 0x00000000 0x00000000 0x00000000 0x00000000 0x00000000 0x00000002 0x00000000 0x00000000 0x00000000 0 C   X X X X X X X X X X X X X X X X 0
0x0000ff00 0x00000000 0x00000000 0x00000000 0x00000000 0x00000000 0x00000000 0x00000000 0x00000002 0x00000000 0x00000000 0x00000000 0 C   X X X X X X X X X X X X X X X X 0
0x0000ff00 0x00000000 0x00000000 0x00000000 0x00000000 0x00000000 0x00000000 0x00000000 0x00000002 0x00000000 0x00000000 0x00000000 0 C   X X X X X X X X X X X X X X X X 0
0x0000ff00 0x00000000 0x00000000 0x00000000 0x00000000 0x00000000 0x00000000 0x00000000 0x00000002 0x00000000 0x00000000 0x00000000 0 C   X X X X X X X X X X X X X X X X 0
0x0000ff00 0x00000000 0x00000000 0x00000000 0x00000000 0x00000000 0x00000000 0x00000000 0x00000002 0x00000000 0x00000000 0x00000000 0 C   X X X X X X X X X X X X X X X X 0
0x0000ff00 0x00000000 0x00000000 0x00000000 0x00000000 0x00000000 0x00000000 0x00000000 0x00000002 0x00000000 0x00000000 0x00000000 0 C   X X X X X X X X X X X X X X X X 0
0x0000ff00 0x00000000 0x00000000 0x00000000 0x00000000 0x00000000 0x00000000 0x00000000 0x00000002 0x00000000 0x00000000 0x00000000 0 C   0xfb4dd572 0x4bc42ef1 0xdf922636 0x327f1394 0xa78dea8f 0x5e269039 0xa1bebbc1 0xcaf09aae 0xa25ab213 0x48a6b46c 0x1b9d9bcb 0x092c5be6 0x546ca624 0x1bec45d5 0x87f47473 0x96f0992e 1
*/

/* Test case A.1 #5:
k0 k1 k2 k3 k4 k5 k6 k7 bc n0 n1 n2 start clk   o0 o1 o2 o3 o4 o5 o6 o7 o8 o9 o10 o11 o12 o13 o14 o15 done

# RFC 8439 A.1, test vector #5: block counter 0
0x00000000 0x00000000 0x00000000 0x00000000 0x00000000 0x00000000 0x00000000 0x00000000 0x00000000 0x00000000 0x00000000 0x02000000 1 C   X X X X X X X X X X X X X X X X 0
0x00000000 0x00000000 0x00000000 0x00000000 0x00000000 0x00000000 0x00000000 0x00000000 0x00000000 0x00000000 0x00000000 0x02000000 0 C   X X X X X X X X X X X X X X X X 0
0x00000000 0x00000000 0x00000000 0x00000000 0x00000000 0x00000000 0x00000000 0x00000000 0x00000000 0x00000000 0x00000000 0x02000000 0 C   X X X X X X X X X X X X X X X X 0
0x00000000 0x00000000 0x00000000 0x00000000 0x00000000 0x00000000 0x00000000 0x00000000 0x00000000 0x00000000 0x00000000 0x02000000 0 C   X X X X X X X X X X X X X X X X 0
0x00000000 0x00000000 0x00000000 0x00000000 0x00000000 0x00000000 0x00000000 0x00000000 0x00000000 0x00000000 0x00000000 0x02000000 0 C   X X X X X X X X X X X X X X X X 0
0x00000000 0x00000000 0x00000000 0x00000000 0x00000000 0x00000000 0x00000000 0x00000000 0x00000000 0x00000000 0x00000000 0x02000000 0 C   X X X X X X X X X X X X X X X X 0
0x00000000 0x00000000 0x00000000 0x00000000 0x00000000 0x00000000 0x00000000 0x00000000 0x00000000 0x00000000 0x00000000 0x02000000 0 C   X X X X X X X X X X X X X X X X 0
0x00000000 0x00000000 0x00000000 0x00000000 0x00000000 0x00000000 0x00000000 0x00000000 0x00000000 0x00000000 0x00000000 0x02000000 0 C   X X X X X X X X X X X X X X X X 0
0x00000000 0x00000000 0x00000000 0x00000000 0x00000000 0x00000000 0x00000000 0x00000000 0x00000000 0x00000000 0x00000000 0x02000000 0 C   X X X X X X X X X X X X X X X X 0
0x00000000 0x00000000 0x00000000 0x00000000 0x00000000 0x00000000 0x00000000 0x00000000 0x00000000 0x00000000 0x00000000 0x02000000 0 C   0x374dc6c2 0x3736d58c 0xb904e24a 0xcd3f93ef 0x88228b1a 0x96a4dfb3 0x5b76ab72 0xc727ee54 0x0e0e978a 0xf3145c95 0x1b748ea8 0xf786c297 0x99c28f5f 0x628314e8 0x398a19fa 0x6ded1b53 1
*/
