// Digital circuit core.dig as structural Verilog
module core (
  input  [31:0] k1,
  input  [31:0] k2,
  input  [31:0] k3,
  input  [31:0] k4,
  input  [31:0] k5,
  input  [31:0] k6,
  input  [31:0] k7,
  input  [31:0] k0,
  input  [31:0] n0,
  input  [31:0] n1,
  input  [31:0] n2,
  input  rst,
  input  start,
  input  [31:0] counter0,
  input  [31:0] in__data,
  input  in__valid,
  input  in__last,
  input  [3:0] in__keep,
  input  CLK,
  input  out__ready,
  output [31:0] out__data,
  output out__valid,
  output out__last,
  output [3:0] out__keep,
  output in__ready,
  output error
);

  wire acc, avail, bccarry, bstart, capd, capgen, capx, cb, done, dr, genacc, hs, ks__capture, load, navail,
       ncb, nlast, nload, novf, or_1_out, or_2_out, ovf, ovn, ovo, ovs, rdy, rdyn, st__gen, st__idle,
       st__xor, w15, w15gen, w__inc, wrap, wrapn;
  wire [3:0] add_2_s, multiplexer_1_out, w;
  wire [31:0] add_1_s, bc, bcblk, k0b, k0l, k1b, k1l, k2b, k2l, k3b, k3l, k4b, k4l, k5b, k5l, k6b, k6l, k7b,
       k7l, ks__word, kwx, multiplexer_2_out, n0b, n0l, n1b, n1l, n2b, n2l, o0, o1, o2, o3, o4, o5, o6, o7,
       o8, o9, o10, o11, o12, o13, o14, o15, ow, register_1_q, register_2_q, register_3_q, register_4_q,
       register_7_q, register_8_q, register_9_q, register_10_q, register_11_q, register_12_q, register_13_q,
       register_14_q, register_15_q, register_16_q, register_17_q, register_18_q;

  Add #(.Bits(32)) add_1 (.a(bc), .b(32'h1), .c_i(1'b0), .s(add_1_s), .c_o(bccarry));
  Add #(.Bits(4)) add_2 (.a(w), .b(4'b0001), .c_i(1'b0), .s(add_2_s));  // open: c_o
  Register #(.Bits(32)) register_1 (.D(o0), .C(CLK), .en(ks__capture), .Q(register_1_q));
  Register #(.Bits(32)) register_2 (.D(o1), .C(CLK), .en(ks__capture), .Q(register_2_q));
  Multiplexer #(.Bits(4)) multiplexer_1 (.sel(w__inc), .in_0(4'b0000), .in_1(add_2_s), .out(multiplexer_1_out));
  or or_1 (or_1_out, load, w__inc);
  Register #(.Bits(32)) register_3 (.D(o2), .C(CLK), .en(ks__capture), .Q(register_3_q));
  Multiplexer #(.Bits(32)) multiplexer_2 (.sel(ks__capture), .in_0(counter0), .in_1(add_1_s), .out(multiplexer_2_out));
  or or_2 (or_2_out, load, ks__capture);
  Register #(.Bits(32)) register_4 (.D(o3), .C(CLK), .en(ks__capture), .Q(register_4_q));
  Register #(.Bits(32)) register_5 (.D(multiplexer_2_out), .C(CLK), .en(or_2_out), .Q(bc));
  Register #(.Bits(4)) register_6 (.D(multiplexer_1_out), .C(CLK), .en(or_1_out), .Q(w));
  and and_1 (w15, w[0], w[1], w[2], w[3]);
  Register #(.Bits(32)) register_7 (.D(o4), .C(CLK), .en(ks__capture), .Q(register_7_q));
  ctrl ctrl_1 (
    .done(avail), .hs(hs), .last(in__last), .start(start), .w15(w15gen), .C(CLK), .rst(rst),
    .st_gen(st__gen), .st_idle(st__idle), .st_xor(st__xor));
  Register #(.Bits(32)) register_8 (.D(o5), .C(CLK), .en(ks__capture), .Q(register_8_q));
  block_function block_function_1 (
    .k0(k0b), .k1(k1b), .k2(k2b), .k3(k3b), .k4(k4b), .k5(k5b), .k6(k6b), .k7(k7b), .n0(n0b), .n1(n1b),
    .n2(n2b), .start(bstart), .clk(CLK), .o0(o0), .o1(o1), .o2(o2), .o3(o3), .o4(o4), .o5(o5), .o6(o6),
    .o7(o7), .o8(o8), .o9(o9), .o10(o10), .o11(o11), .o12(o12), .o13(o13), .o14(o14), .o15(o15), .done(done));  // open: bc
  Register #(.Bits(32)) register_9 (.D(o6), .C(CLK), .en(ks__capture), .Q(register_9_q));
  Register #(.Bits(32)) register_10 (.D(o7), .C(CLK), .en(ks__capture), .Q(register_10_q));
  Register #(.Bits(32)) register_11 (.D(o8), .C(CLK), .en(ks__capture), .Q(register_11_q));
  Register #(.Bits(32)) register_12 (.D(o9), .C(CLK), .en(ks__capture), .Q(register_12_q));
  and and_2 (in__ready, acc, out__ready);
  and and_3 (out__valid, acc, in__valid);
  and and_4 (hs, in__valid, in__ready);
  and and_5 (load, st__idle, start);
  Register #(.Bits(32)) register_13 (.D(o10), .C(CLK), .en(ks__capture), .Q(register_13_q));
  Register #(.Bits(32)) register_14 (.D(o11), .C(CLK), .en(ks__capture), .Q(register_14_q));
  Register #(.Bits(32)) register_15 (.D(o12), .C(CLK), .en(ks__capture), .Q(register_15_q));
  assign out__data = in__data ^ kwx;  // XOr xor_1, 32 bits wide
  Register #(.Bits(32)) register_16 (.D(o13), .C(CLK), .en(ks__capture), .Q(register_16_q));
  and and_6 (capgen, st__gen, avail);
  and and_7 (w__inc, acc, hs);
  and and_8 (wrap, hs, st__xor, w15);
  Register #(.Bits(32)) register_17 (.D(o14), .C(CLK), .en(ks__capture), .Q(register_17_q));
  Register #(.Bits(32)) register_18 (.D(o15), .C(CLK), .en(ks__capture), .Q(register_18_q));
  Multiplexer #(.Selector_Bits(4), .Bits(32)) multiplexer_3 (
    .sel(w), .in_0(register_1_q), .in_1(register_2_q), .in_2(register_3_q), .in_3(register_4_q),
    .in_4(register_7_q), .in_5(register_8_q), .in_6(register_9_q), .in_7(register_10_q),
    .in_8(register_11_q), .in_9(register_12_q), .in_10(register_13_q), .in_11(register_14_q),
    .in_12(register_15_q), .in_13(register_16_q), .in_14(register_17_q), .in_15(register_18_q), .out(ks__word));
  or or_3 (dr, done, rdy);
  not not_1 (navail, avail);
  and and_9 (w15gen, w15, navail);
  not not_2 (nlast, in__last);
  and and_10 (wrapn, wrap, nlast);
  and and_11 (capx, wrapn, avail);
  or or_4 (ks__capture, capgen, capx);
  Register #(.Bits(32)) register_19 (.D(k0), .C(CLK), .en(load), .Q(k0l));
  Register #(.Bits(32)) register_20 (.D(k1), .C(CLK), .en(load), .Q(k1l));
  Register #(.Bits(32)) register_21 (.D(k2), .C(CLK), .en(load), .Q(k2l));
  Register #(.Bits(32)) register_22 (.D(k3), .C(CLK), .en(load), .Q(k3l));
  Register #(.Bits(32)) register_23 (.D(k4), .C(CLK), .en(load), .Q(k4l));
  Register #(.Bits(32)) register_24 (.D(k5), .C(CLK), .en(load), .Q(k5l));
  Register #(.Bits(32)) register_25 (.D(k6), .C(CLK), .en(load), .Q(k6l));
  Register #(.Bits(32)) register_26 (.D(k7), .C(CLK), .en(load), .Q(k7l));
  Register #(.Bits(32)) register_27 (.D(n0), .C(CLK), .en(load), .Q(n0l));
  Register #(.Bits(32)) register_28 (.D(n1), .C(CLK), .en(load), .Q(n1l));
  Register #(.Bits(32)) register_29 (.D(n2), .C(CLK), .en(load), .Q(n2l));
  Multiplexer #(.Bits(32)) multiplexer_4 (.sel(st__idle), .in_0(k0l), .in_1(k0), .out(k0b));
  Multiplexer #(.Bits(32)) multiplexer_5 (.sel(st__idle), .in_0(k1l), .in_1(k1), .out(k1b));
  Multiplexer #(.Bits(32)) multiplexer_6 (.sel(st__idle), .in_0(k2l), .in_1(k2), .out(k2b));
  Multiplexer #(.Bits(32)) multiplexer_7 (.sel(st__idle), .in_0(k3l), .in_1(k3), .out(k3b));
  Multiplexer #(.Bits(32)) multiplexer_8 (.sel(st__idle), .in_0(k4l), .in_1(k4), .out(k4b));
  Multiplexer #(.Bits(32)) multiplexer_9 (.sel(st__idle), .in_0(k5l), .in_1(k5), .out(k5b));
  Multiplexer #(.Bits(32)) multiplexer_10 (.sel(st__idle), .in_0(k6l), .in_1(k6), .out(k6b));
  Multiplexer #(.Bits(32)) multiplexer_11 (.sel(st__idle), .in_0(k7l), .in_1(k7), .out(k7b));
  Multiplexer #(.Bits(32)) multiplexer_12 (.sel(st__idle), .in_0(n0l), .in_1(n0), .out(n0b));
  Multiplexer #(.Bits(32)) multiplexer_13 (.sel(st__idle), .in_0(n1l), .in_1(n1), .out(n1b));
  Multiplexer #(.Bits(32)) multiplexer_14 (.sel(st__idle), .in_0(n2l), .in_1(n2), .out(n2b));
  D_FF u_capd (.D(ks__capture), .C(CLK), .Q(capd));  // open: nQ
  or or_5 (bstart, load, capd);
  Multiplexer #(.Bits(32)) multiplexer_15 (.sel(st__idle), .in_0(bc), .in_1(counter0), .out(bcblk));
  or or_6 (cb, ks__capture, bstart);
  not not_3 (ncb, cb);
  and and_12 (rdyn, avail, ncb);
  D_FF u_rdy (.D(rdyn), .C(CLK), .Q(rdy));  // open: nQ
  and and_13 (genacc, st__gen, avail);
  or or_7 (acc, st__xor, genacc);
  Multiplexer #(.Selector_Bits(4), .Bits(32)) multiplexer_16 (
    .sel(w), .in_0(o0), .in_1(o1), .in_2(o2), .in_3(o3), .in_4(o4), .in_5(o5), .in_6(o6), .in_7(o7),
    .in_8(o8), .in_9(o9), .in_10(o10), .in_11(o11), .in_12(o12), .in_13(o13), .in_14(o14), .in_15(o15),
    .out(ow));
  Multiplexer #(.Bits(32)) multiplexer_17 (.sel(st__gen), .in_0(ks__word), .in_1(ow), .out(kwx));
  and and_14 (avail, dr, novf);
  and and_15 (ovs, ks__capture, bccarry);
  or or_8 (ovo, ovs, ovf);
  not not_4 (nload, load);
  and and_16 (ovn, ovo, nload);
  D_FF u_ovf (.D(ovn), .C(CLK), .Q(ovf), .nQ(novf));
  and and_17 (error, ovf, st__gen);

  assign out__keep = in__keep;
  assign out__last = in__last;

  // Other names for the same wires on the sheet: k0in[31:0] = k0; k1in[31:0] = k1; k2in[31:0] = k2; k3in[31:0] = k3;
  //   k4in[31:0] = k4; k5in[31:0] = k5; k6in[31:0] = k6; k7in[31:0] = k7; n0in[31:0] = n0; n1in[31:0] = n1;
  //   n2in[31:0] = n2

  // Notes on the sheet:
  //   ChaCha20
  //   Encryption Algorithm
  //   Block Counter
  //   Word Counter
  //   Keystream Register
  //   State Machine
  //   Glue Logic
  //   Data XOR
  //   Pass-throughts
  //   Inputs
  //   Outputs
  //   Block Prefetch
  //   Key and Nonce Registers
  //   First Word Bypass
  //   Counter Overflow
endmodule

/* Test case test0:
rst CLK start counter0 in\_valid in\_last in\_keep out\_ready in\_data k0 k1 k2 k3 k4 k5 k6 k7 n0 n1 n2   out\_data out\_valid out\_last out\_keep in\_ready

# reset, then start (IDLE -> GEN -> XOR)
1 C 0 1 0 0 0 1 0 0x03020100 0x07060504 0x0b0a0908 0x0f0e0d0c 0x13121110 0x17161514 0x1b1a1918 0x1f1e1d1c 0x00000000 0x4a000000 0x00000000   X X X X X
# (after start the key, nonce and counter0 pins carry garbage until the message ends)
0 C 1 1 0 0 0 1 0 0x03020100 0x07060504 0x0b0a0908 0x0f0e0d0c 0x13121110 0x17161514 0x1b1a1918 0x1f1e1d1c 0x00000000 0x4a000000 0x00000000   X X X X 0
# GEN: 9 more clocks while the block computes; after the last one the keystream is ready
0 C 0 7 0 0 0 1 0 0xdeadbeef 0x01234567 0x89abcdef 0xfeedface 0x0badf00d 0xcafebabe 0x13579bdf 0x2468ace0 0x11111111 0x22222222 0x33333333   X X X X 0
0 C 0 7 0 0 0 1 0 0xdeadbeef 0x01234567 0x89abcdef 0xfeedface 0x0badf00d 0xcafebabe 0x13579bdf 0x2468ace0 0x11111111 0x22222222 0x33333333   X X X X 0
0 C 0 7 0 0 0 1 0 0xdeadbeef 0x01234567 0x89abcdef 0xfeedface 0x0badf00d 0xcafebabe 0x13579bdf 0x2468ace0 0x11111111 0x22222222 0x33333333   X X X X 0
0 C 0 7 0 0 0 1 0 0xdeadbeef 0x01234567 0x89abcdef 0xfeedface 0x0badf00d 0xcafebabe 0x13579bdf 0x2468ace0 0x11111111 0x22222222 0x33333333   X X X X 0
0 C 0 7 0 0 0 1 0 0xdeadbeef 0x01234567 0x89abcdef 0xfeedface 0x0badf00d 0xcafebabe 0x13579bdf 0x2468ace0 0x11111111 0x22222222 0x33333333   X X X X 0
0 C 0 7 0 0 0 1 0 0xdeadbeef 0x01234567 0x89abcdef 0xfeedface 0x0badf00d 0xcafebabe 0x13579bdf 0x2468ace0 0x11111111 0x22222222 0x33333333   X X X X 0
0 C 0 7 0 0 0 1 0 0xdeadbeef 0x01234567 0x89abcdef 0xfeedface 0x0badf00d 0xcafebabe 0x13579bdf 0x2468ace0 0x11111111 0x22222222 0x33333333   X X X X 0
0 C 0 7 0 0 0 1 0 0xdeadbeef 0x01234567 0x89abcdef 0xfeedface 0x0badf00d 0xcafebabe 0x13579bdf 0x2468ace0 0x11111111 0x22222222 0x33333333   X X X X 0
0 C 0 7 0 0 0 1 0 0xdeadbeef 0x01234567 0x89abcdef 0xfeedface 0x0badf00d 0xcafebabe 0x13579bdf 0x2468ace0 0x11111111 0x22222222 0x33333333   X X X X 1
# word 0
0 0 0 7 1 0 15 1 0x6964614c 0xdeadbeef 0x01234567 0x89abcdef 0xfeedface 0x0badf00d 0xcafebabe 0x13579bdf 0x2468ace0 0x11111111 0x22222222 0x33333333   0x9a352e6e 1 0 15 1
0 C 0 7 1 0 15 1 0x6964614c 0xdeadbeef 0x01234567 0x89abcdef 0xfeedface 0x0badf00d 0xcafebabe 0x13579bdf 0x2468ace0 0x11111111 0x22222222 0x33333333   X X X X X
# word 1
0 0 0 7 1 0 15 1 0x61207365 0xdeadbeef 0x01234567 0x89abcdef 0xfeedface 0x0badf00d 0xcafebabe 0x13579bdf 0x2468ace0 0x11111111 0x22222222 0x33333333   0x80f96825 1 0 15 1
0 C 0 7 1 0 15 1 0x61207365 0xdeadbeef 0x01234567 0x89abcdef 0xfeedface 0x0badf00d 0xcafebabe 0x13579bdf 0x2468ace0 0x11111111 0x22222222 0x33333333   X X X X X
# word 2
0 0 0 7 1 0 15 1 0x4720646e 0xdeadbeef 0x01234567 0x89abcdef 0xfeedface 0x0badf00d 0xcafebabe 0x13579bdf 0x2468ace0 0x11111111 0x22222222 0x33333333   0x2807ba41 1 0 15 1
0 C 0 7 1 0 15 1 0x4720646e 0xdeadbeef 0x01234567 0x89abcdef 0xfeedface 0x0badf00d 0xcafebabe 0x13579bdf 0x2468ace0 0x11111111 0x22222222 0x33333333   X X X X X
# word 3
0 0 0 7 1 0 15 1 0x6c746e65 0xdeadbeef 0x01234567 0x89abcdef 0xfeedface 0x0badf00d 0xcafebabe 0x13579bdf 0x2468ace0 0x11111111 0x22222222 0x33333333   0x81690ddd 1 0 15 1
0 C 0 7 1 0 15 1 0x6c746e65 0xdeadbeef 0x01234567 0x89abcdef 0xfeedface 0x0badf00d 0xcafebabe 0x13579bdf 0x2468ace0 0x11111111 0x22222222 0x33333333   X X X X X
# word 4
0 0 0 7 1 0 15 1 0x6e656d65 0xdeadbeef 0x01234567 0x89abcdef 0xfeedface 0x0badf00d 0xcafebabe 0x13579bdf 0x2468ace0 0x11111111 0x22222222 0x33333333   0xec7a7ee9 1 0 15 1
0 C 0 7 1 0 15 1 0x6e656d65 0xdeadbeef 0x01234567 0x89abcdef 0xfeedface 0x0badf00d 0xcafebabe 0x13579bdf 0x2468ace0 0x11111111 0x22222222 0x33333333   X X X X X
# word 5
0 0 0 7 1 0 15 1 0x20666f20 0xdeadbeef 0x01234567 0x89abcdef 0xfeedface 0x0badf00d 0xcafebabe 0x13579bdf 0x2468ace0 0x11111111 0x22222222 0x33333333   0xc260431d 1 0 15 1
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*/

/* Test case overflow:
rst CLK start counter0 in\_valid in\_last in\_keep out\_ready in\_data k0 k1 k2 k3 k4 k5 k6 k7 n0 n1 n2   out\_data out\_valid in\_ready error

# reset, start at the last block counter
1 C 0 0 0 0 15 1 0x00000000 0x03020100 0x07060504 0x0b0a0908 0x0f0e0d0c 0x13121110 0x17161514 0x1b1a1918 0x1f1e1d1c 0x00000000 0x4a000000 0x00000000   X X X 0
0 C 1 4294967295 0 0 15 1 0x00000000 0x03020100 0x07060504 0x0b0a0908 0x0f0e0d0c 0x13121110 0x17161514 0x1b1a1918 0x1f1e1d1c 0x00000000 0x4a000000 0x00000000   X X 0 0
# GEN: block 0xffffffff
0 C 0 4294967295 0 0 15 1 0x00000000 0x03020100 0x07060504 0x0b0a0908 0x0f0e0d0c 0x13121110 0x17161514 0x1b1a1918 0x1f1e1d1c 0x00000000 0x4a000000 0x00000000   X 0 0 0
0 C 0 4294967295 0 0 15 1 0x00000000 0x03020100 0x07060504 0x0b0a0908 0x0f0e0d0c 0x13121110 0x17161514 0x1b1a1918 0x1f1e1d1c 0x00000000 0x4a000000 0x00000000   X 0 0 0
0 C 0 4294967295 0 0 15 1 0x00000000 0x03020100 0x07060504 0x0b0a0908 0x0f0e0d0c 0x13121110 0x17161514 0x1b1a1918 0x1f1e1d1c 0x00000000 0x4a000000 0x00000000   X 0 0 0
0 C 0 4294967295 0 0 15 1 0x00000000 0x03020100 0x07060504 0x0b0a0908 0x0f0e0d0c 0x13121110 0x17161514 0x1b1a1918 0x1f1e1d1c 0x00000000 0x4a000000 0x00000000   X 0 0 0
0 C 0 4294967295 0 0 15 1 0x00000000 0x03020100 0x07060504 0x0b0a0908 0x0f0e0d0c 0x13121110 0x17161514 0x1b1a1918 0x1f1e1d1c 0x00000000 0x4a000000 0x00000000   X 0 0 0
0 C 0 4294967295 0 0 15 1 0x00000000 0x03020100 0x07060504 0x0b0a0908 0x0f0e0d0c 0x13121110 0x17161514 0x1b1a1918 0x1f1e1d1c 0x00000000 0x4a000000 0x00000000   X 0 0 0
0 C 0 4294967295 0 0 15 1 0x00000000 0x03020100 0x07060504 0x0b0a0908 0x0f0e0d0c 0x13121110 0x17161514 0x1b1a1918 0x1f1e1d1c 0x00000000 0x4a000000 0x00000000   X 0 0 0
0 C 0 4294967295 0 0 15 1 0x00000000 0x03020100 0x07060504 0x0b0a0908 0x0f0e0d0c 0x13121110 0x17161514 0x1b1a1918 0x1f1e1d1c 0x00000000 0x4a000000 0x00000000   X 0 0 0
0 C 0 4294967295 0 0 15 1 0x00000000 0x03020100 0x07060504 0x0b0a0908 0x0f0e0d0c 0x13121110 0x17161514 0x1b1a1918 0x1f1e1d1c 0x00000000 0x4a000000 0x00000000   X 0 1 0
# word 0
0 0 0 4294967295 1 0 15 1 0x6964614c 0x03020100 0x07060504 0x0b0a0908 0x0f0e0d0c 0x13121110 0x17161514 0x1b1a1918 0x1f1e1d1c 0x00000000 0x4a000000 0x00000000   0x32be4821 1 1 0
0 C 0 4294967295 1 0 15 1 0x6964614c 0x03020100 0x07060504 0x0b0a0908 0x0f0e0d0c 0x13121110 0x17161514 0x1b1a1918 0x1f1e1d1c 0x00000000 0x4a000000 0x00000000   X X X X
# word 1
0 0 0 4294967295 1 0 15 1 0x6964614d 0x03020100 0x07060504 0x0b0a0908 0x0f0e0d0c 0x13121110 0x17161514 0x1b1a1918 0x1f1e1d1c 0x00000000 0x4a000000 0x00000000   0x40230b9c 1 1 0
0 C 0 4294967295 1 0 15 1 0x6964614d 0x03020100 0x07060504 0x0b0a0908 0x0f0e0d0c 0x13121110 0x17161514 0x1b1a1918 0x1f1e1d1c 0x00000000 0x4a000000 0x00000000   X X X X
# word 2
0 0 0 4294967295 1 0 15 1 0x6964614e 0x03020100 0x07060504 0x0b0a0908 0x0f0e0d0c 0x13121110 0x17161514 0x1b1a1918 0x1f1e1d1c 0x00000000 0x4a000000 0x00000000   0xd4a4895e 1 1 0
0 C 0 4294967295 1 0 15 1 0x6964614e 0x03020100 0x07060504 0x0b0a0908 0x0f0e0d0c 0x13121110 0x17161514 0x1b1a1918 0x1f1e1d1c 0x00000000 0x4a000000 0x00000000   X X X X
# word 3
0 0 0 4294967295 1 0 15 1 0x6964614f 0x03020100 0x07060504 0x0b0a0908 0x0f0e0d0c 0x13121110 0x17161514 0x1b1a1918 0x1f1e1d1c 0x00000000 0x4a000000 0x00000000   0xa1bb1ffb 1 1 0
0 C 0 4294967295 1 0 15 1 0x6964614f 0x03020100 0x07060504 0x0b0a0908 0x0f0e0d0c 0x13121110 0x17161514 0x1b1a1918 0x1f1e1d1c 0x00000000 0x4a000000 0x00000000   X X X X
# word 4
0 0 0 4294967295 1 0 15 1 0x69646150 0x03020100 0x07060504 0x0b0a0908 0x0f0e0d0c 0x13121110 0x17161514 0x1b1a1918 0x1f1e1d1c 0x00000000 0x4a000000 0x00000000   0x4b56fd19 1 1 0
0 C 0 4294967295 1 0 15 1 0x69646150 0x03020100 0x07060504 0x0b0a0908 0x0f0e0d0c 0x13121110 0x17161514 0x1b1a1918 0x1f1e1d1c 0x00000000 0x4a000000 0x00000000   X X X X
# word 5
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*/

/* Test case A.2 #1:
rst CLK start counter0 in\_valid in\_last in\_keep out\_ready in\_data k0 k1 k2 k3 k4 k5 k6 k7 n0 n1 n2   out\_data out\_valid out\_last out\_keep in\_ready error

# RFC 8439 A.2, test vector #1: 64 bytes, initial block counter 0
1 C 0 0 0 0 0 1 0x00000000 0x00000000 0x00000000 0x00000000 0x00000000 0x00000000 0x00000000 0x00000000 0x00000000 0x00000000 0x00000000 0x00000000   X X X X X 0
0 C 1 0 0 0 0 1 0x00000000 0x00000000 0x00000000 0x00000000 0x00000000 0x00000000 0x00000000 0x00000000 0x00000000 0x00000000 0x00000000 0x00000000   X X X X 0 0
0 C 0 0 0 0 0 1 0x00000000 0x00000000 0x00000000 0x00000000 0x00000000 0x00000000 0x00000000 0x00000000 0x00000000 0x00000000 0x00000000 0x00000000   X 0 X X 0 0
0 C 0 0 0 0 0 1 0x00000000 0x00000000 0x00000000 0x00000000 0x00000000 0x00000000 0x00000000 0x00000000 0x00000000 0x00000000 0x00000000 0x00000000   X 0 X X 0 0
0 C 0 0 0 0 0 1 0x00000000 0x00000000 0x00000000 0x00000000 0x00000000 0x00000000 0x00000000 0x00000000 0x00000000 0x00000000 0x00000000 0x00000000   X 0 X X 0 0
0 C 0 0 0 0 0 1 0x00000000 0x00000000 0x00000000 0x00000000 0x00000000 0x00000000 0x00000000 0x00000000 0x00000000 0x00000000 0x00000000 0x00000000   X 0 X X 0 0
0 C 0 0 0 0 0 1 0x00000000 0x00000000 0x00000000 0x00000000 0x00000000 0x00000000 0x00000000 0x00000000 0x00000000 0x00000000 0x00000000 0x00000000   X 0 X X 0 0
0 C 0 0 0 0 0 1 0x00000000 0x00000000 0x00000000 0x00000000 0x00000000 0x00000000 0x00000000 0x00000000 0x00000000 0x00000000 0x00000000 0x00000000   X 0 X X 0 0
0 C 0 0 0 0 0 1 0x00000000 0x00000000 0x00000000 0x00000000 0x00000000 0x00000000 0x00000000 0x00000000 0x00000000 0x00000000 0x00000000 0x00000000   X 0 X X 0 0
0 C 0 0 0 0 0 1 0x00000000 0x00000000 0x00000000 0x00000000 0x00000000 0x00000000 0x00000000 0x00000000 0x00000000 0x00000000 0x00000000 0x00000000   X 0 X X 0 0
0 C 0 0 0 0 0 1 0x00000000 0x00000000 0x00000000 0x00000000 0x00000000 0x00000000 0x00000000 0x00000000 0x00000000 0x00000000 0x00000000 0x00000000   X 0 X X 1 0
# block 0
0 0 0 0 1 0 15 1 0x00000000 0x00000000 0x00000000 0x00000000 0x00000000 0x00000000 0x00000000 0x00000000 0x00000000 0x00000000 0x00000000 0x00000000   0xade0b876 1 0 15 1 0
0 C 0 0 1 0 15 1 0x00000000 0x00000000 0x00000000 0x00000000 0x00000000 0x00000000 0x00000000 0x00000000 0x00000000 0x00000000 0x00000000 0x00000000   X X X X X X
0 0 0 0 1 0 15 1 0x00000000 0x00000000 0x00000000 0x00000000 0x00000000 0x00000000 0x00000000 0x00000000 0x00000000 0x00000000 0x00000000 0x00000000   0x903df1a0 1 0 15 1 0
0 C 0 0 1 0 15 1 0x00000000 0x00000000 0x00000000 0x00000000 0x00000000 0x00000000 0x00000000 0x00000000 0x00000000 0x00000000 0x00000000 0x00000000   X X X X X X
0 0 0 0 1 0 15 1 0x00000000 0x00000000 0x00000000 0x00000000 0x00000000 0x00000000 0x00000000 0x00000000 0x00000000 0x00000000 0x00000000 0x00000000   0xe56a5d40 1 0 15 1 0
0 C 0 0 1 0 15 1 0x00000000 0x00000000 0x00000000 0x00000000 0x00000000 0x00000000 0x00000000 0x00000000 0x00000000 0x00000000 0x00000000 0x00000000   X X X X X X
0 0 0 0 1 0 15 1 0x00000000 0x00000000 0x00000000 0x00000000 0x00000000 0x00000000 0x00000000 0x00000000 0x00000000 0x00000000 0x00000000 0x00000000   0x28bd8653 1 0 15 1 0
0 C 0 0 1 0 15 1 0x00000000 0x00000000 0x00000000 0x00000000 0x00000000 0x00000000 0x00000000 0x00000000 0x00000000 0x00000000 0x00000000 0x00000000   X X X X X X
0 0 0 0 1 0 15 1 0x00000000 0x00000000 0x00000000 0x00000000 0x00000000 0x00000000 0x00000000 0x00000000 0x00000000 0x00000000 0x00000000 0x00000000   0xb819d2bd 1 0 15 1 0
0 C 0 0 1 0 15 1 0x00000000 0x00000000 0x00000000 0x00000000 0x00000000 0x00000000 0x00000000 0x00000000 0x00000000 0x00000000 0x00000000 0x00000000   X X X X X X
0 0 0 0 1 0 15 1 0x00000000 0x00000000 0x00000000 0x00000000 0x00000000 0x00000000 0x00000000 0x00000000 0x00000000 0x00000000 0x00000000 0x00000000   0x1aed8da0 1 0 15 1 0
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*/

/* Test case A.2 #2:
rst CLK start counter0 in\_valid in\_last in\_keep out\_ready in\_data k0 k1 k2 k3 k4 k5 k6 k7 n0 n1 n2   out\_data out\_valid out\_last out\_keep in\_ready error

# RFC 8439 A.2, test vector #2: 375 bytes, initial block counter 1
1 C 0 1 0 0 0 1 0x00000000 0x00000000 0x00000000 0x00000000 0x00000000 0x00000000 0x00000000 0x00000000 0x01000000 0x00000000 0x00000000 0x02000000   X X X X X 0
0 C 1 1 0 0 0 1 0x00000000 0x00000000 0x00000000 0x00000000 0x00000000 0x00000000 0x00000000 0x00000000 0x01000000 0x00000000 0x00000000 0x02000000   X X X X 0 0
0 C 0 1 0 0 0 1 0x00000000 0x00000000 0x00000000 0x00000000 0x00000000 0x00000000 0x00000000 0x00000000 0x01000000 0x00000000 0x00000000 0x02000000   X 0 X X 0 0
0 C 0 1 0 0 0 1 0x00000000 0x00000000 0x00000000 0x00000000 0x00000000 0x00000000 0x00000000 0x00000000 0x01000000 0x00000000 0x00000000 0x02000000   X 0 X X 0 0
0 C 0 1 0 0 0 1 0x00000000 0x00000000 0x00000000 0x00000000 0x00000000 0x00000000 0x00000000 0x00000000 0x01000000 0x00000000 0x00000000 0x02000000   X 0 X X 0 0
0 C 0 1 0 0 0 1 0x00000000 0x00000000 0x00000000 0x00000000 0x00000000 0x00000000 0x00000000 0x00000000 0x01000000 0x00000000 0x00000000 0x02000000   X 0 X X 0 0
0 C 0 1 0 0 0 1 0x00000000 0x00000000 0x00000000 0x00000000 0x00000000 0x00000000 0x00000000 0x00000000 0x01000000 0x00000000 0x00000000 0x02000000   X 0 X X 0 0
0 C 0 1 0 0 0 1 0x00000000 0x00000000 0x00000000 0x00000000 0x00000000 0x00000000 0x00000000 0x00000000 0x01000000 0x00000000 0x00000000 0x02000000   X 0 X X 0 0
0 C 0 1 0 0 0 1 0x00000000 0x00000000 0x00000000 0x00000000 0x00000000 0x00000000 0x00000000 0x00000000 0x01000000 0x00000000 0x00000000 0x02000000   X 0 X X 0 0
0 C 0 1 0 0 0 1 0x00000000 0x00000000 0x00000000 0x00000000 0x00000000 0x00000000 0x00000000 0x00000000 0x01000000 0x00000000 0x00000000 0x02000000   X 0 X X 0 0
0 C 0 1 0 0 0 1 0x00000000 0x00000000 0x00000000 0x00000000 0x00000000 0x00000000 0x00000000 0x00000000 0x01000000 0x00000000 0x00000000 0x02000000   X 0 X X 1 0
# block 1
0 0 0 1 1 0 15 1 0x20796e41 0x00000000 0x00000000 0x00000000 0x00000000 0x00000000 0x00000000 0x00000000 0x01000000 0x00000000 0x00000000 0x02000000   0x7df0fba3 1 0 15 1 0
0 C 0 1 1 0 15 1 0x20796e41 0x00000000 0x00000000 0x00000000 0x00000000 0x00000000 0x00000000 0x00000000 0x01000000 0x00000000 0x00000000 0x02000000   X X X X X X
0 0 0 1 1 0 15 1 0x6d627573 0x00000000 0x00000000 0x00000000 0x00000000 0x00000000 0x00000000 0x00000000 0x01000000 0x00000000 0x00000000 0x02000000   0xde2ffaf3 1 0 15 1 0
0 C 0 1 1 0 15 1 0x6d627573 0x00000000 0x00000000 0x00000000 0x00000000 0x00000000 0x00000000 0x00000000 0x01000000 0x00000000 0x00000000 0x02000000   X X X X X X
0 0 0 1 1 0 15 1 0x69737369 0x00000000 0x00000000 0x00000000 0x00000000 0x00000000 0x00000000 0x00000000 0x01000000 0x00000000 0x00000000 0x02000000   0xa26c374f 1 0 15 1 0
0 C 0 1 1 0 15 1 0x69737369 0x00000000 0x00000000 0x00000000 0x00000000 0x00000000 0x00000000 0x00000000 0x01000000 0x00000000 0x00000000 0x02000000   X X X X X X
0 0 0 1 1 0 15 1 0x74206e6f 0x00000000 0x00000000 0x00000000 0x00000000 0x00000000 0x00000000 0x00000000 0x01000000 0x00000000 0x00000000 0x02000000   0x7073823e 1 0 15 1 0
0 C 0 1 1 0 15 1 0x74206e6f 0x00000000 0x00000000 0x00000000 0x00000000 0x00000000 0x00000000 0x00000000 0x01000000 0x00000000 0x00000000 0x02000000   X X X X X X
0 0 0 1 1 0 15 1 0x6874206f 0x00000000 0x00000000 0x00000000 0x00000000 0x00000000 0x00000000 0x00000000 0x01000000 0x00000000 0x00000000 0x02000000   0x9f5d6041 1 0 15 1 0
0 C 0 1 1 0 15 1 0x6874206f 0x00000000 0x00000000 0x00000000 0x00000000 0x00000000 0x00000000 0x00000000 0x01000000 0x00000000 0x00000000 0x02000000   X X X X X X
0 0 0 1 1 0 15 1 0x45492065 0x00000000 0x00000000 0x00000000 0x00000000 0x00000000 0x00000000 0x00000000 0x01000000 0x00000000 0x00000000 0x02000000   0xbd574f4f 1 0 15 1 0
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*/

/* Test case A.2 #3:
rst CLK start counter0 in\_valid in\_last in\_keep out\_ready in\_data k0 k1 k2 k3 k4 k5 k6 k7 n0 n1 n2   out\_data out\_valid out\_last out\_keep in\_ready error

# RFC 8439 A.2, test vector #3: 127 bytes, initial block counter 42
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*/
