// Digital circuit ctrl.dig as structural Verilog
module ctrl (
  input  done,
  input  hs,
  input  last,
  input  start,
  input  w15,
  input  C,
  input  rst,
  output st_gen,
  output st_idle,
  output st_xor
);

  wire and_1_out, and_2_out, and_3_out, and_4_out, and_5_out, and_6_out, and_8_out, and_9_out, and_10_out,
       nhl, not_1_out, not_2_out, not_3_out, not_4_out, not_5_out, not_6_out, not_7_out, or_1_out, or_2_out;

  not not_1 (not_1_out, done);
  not not_2 (not_2_out, hs);
  not not_3 (not_3_out, last);
  not not_4 (not_4_out, w15);
  not not_5 (not_5_out, st_xor);
  not not_6 (not_6_out, st_gen);
  and and_1 (and_1_out, st_gen, nhl, done);
  and and_2 (and_2_out, st_xor, not_3_out, not_4_out);
  and and_3 (and_3_out, st_xor, not_2_out);
  and and_4 (and_4_out, not_6_out, not_5_out, start);
  and and_5 (and_5_out, st_gen, not_1_out);
  and and_6 (and_6_out, st_xor, hs, not_3_out, w15);
  and and_7 (st_idle, not_6_out, not_5_out);
  or or_1 (or_1_out, and_1_out, and_2_out, and_3_out);
  or or_2 (or_2_out, and_4_out, and_5_out, and_6_out);
  not not_7 (not_7_out, rst);
  and and_8 (and_8_out, not_7_out, or_1_out);
  and and_9 (and_9_out, not_7_out, or_2_out);
  D_FF Z_1_n (.D(and_8_out), .C(C), .Q(st_xor));  // open: nQ
  D_FF Z_0_n (.D(and_9_out), .C(C), .Q(st_gen));  // open: nQ
  // Probe ctrl.fsm on {w15, start, last, hs, done, st_xor, st_gen}
  and and_10 (and_10_out, hs, last);
  not not_8 (nhl, and_10_out);

  // Other names for the same wires on the sheet: Z_0_n = st_gen; Z_1_n = st_xor
endmodule

/* Test case test0:
rst C start done hs last w15   st_idle st_gen st_xor

# reset
1   C   0     0    0  0    0     1       0      0
# IDLE waits for start, ignores other inputs
0   C   0     0    0  0    0     1       0      0
0   C   0     1    1  1    1     1       0      0
# IDLE -> GEN
0   C   1     0    0  0    0     0       1      0
# GEN waits for done
0   C   0     0    0  0    0     0       1      0
0   C   0     0    1  1    1     0       1      0
# GEN -> XOR
0   C   0     1    0  0    0     0       0      1
# XOR: no handshake, stay
0   C   0     0    0  0    0     0       0      1
# XOR: handshake, word < 15, stay
0   C   0     0    1  0    0     0       0      1
# XOR: handshake on word 15 -> GEN (next block)
0   C   0     0    1  0    1     0       1      0
# GEN -> XOR
0   C   0     1    0  0    0     0       0      1
# XOR: last word -> IDLE
0   C   0     0    1  1    0     1       0      0

# last has priority over w15
0   C   1     0    0  0    0     0       1      0
0   C   0     1    0  0    0     0       0      1
0   C   0     0    1  1    1     1       0      0

# last without handshake does nothing
0   C   1     0    0  0    0     0       1      0
0   C   0     1    0  0    0     0       0      1
0   C   0     0    0  1    1     0       0      1

# back to IDLE
1   C   0     0    0  0    0     1       0      0
# GEN: done together with the last word -> IDLE (one-word message)
0   C   1     0    0  0    0     0       1      0
0   C   0     1    1  1    0     1       0      0
# GEN: done together with a word that is not the last -> XOR
0   C   1     0    0  0    0     0       1      0
0   C   0     1    1  0    0     0       0      1
# GEN: done, last but no handshake -> XOR
0   C   0     0    1  1    0     1       0      0
0   C   1     0    0  0    0     0       1      0
0   C   0     1    0  1    0     0       0      1

# reset from XOR
1   C   0     0    0  0    0     1       0      0
*/
